# Fritzing sketch PCB (saved by Fritzing 0.9.0b)
breadboards: 1

parts:
  Part1 = Arduino Nano (Rev3.0)
  D1 = LTE-302 [package=lte-302]
  R1 = Resistor [tolerance=±5% resistance=220 package=THT]

nets:
  N1: Part1.GND, D1.C
  N2: Part1.D3, R1.Pin_1
  N3: D1.A, R1.Pin_0
